# Fritzing sketch Rfid (saved by Fritzing 0.9.3b)

parts:
  U1 = NodeMCU V3.0
  KY-1 = Keyes Relay [package=THT]
  LCD2 = LCD screen
  LCM1602_IIC2 = LCM1602 IIC [part_number="LCM1602 IIC" chip_label="LCM1602 IIC" package="DIP (Dual Inline) [THT]"]
  Parça1 = RFID-RC522 [part_number=101218]
  J1 = Piezo Speaker

nets:
  N1: U1.D0, KY-1.signal
  N2: U1.D1, LCM1602_IIC2.SCL
  N3: U1.D2, LCM1602_IIC2.SDA
  N4: U1.D3, J1.pin2
  N5: U1.D4, Parça1.RST
  3V3: U1.3V3, KY-1.power, Parça1.3.3V
  GND: U1.GND, KY-1.ground, LCM1602_IIC2.GND, Parça1.GND, J1.pin1
  N6: U1.D5, Parça1.SCK
  N7: U1.D6, Parça1.MISO
  N8: U1.D7, Parça1.MOSI
  N9: U1.D8, Parça1.SDA
  VIN: U1.Vin, LCM1602_IIC2.VCC
  VSS: LCD2.VSS, LCM1602_IIC2.VSS
  VDD: LCD2.VDD, LCM1602_IIC2.VDD
  N10: LCD2.V0, LCM1602_IIC2.V0
  N11: LCD2.RS, LCM1602_IIC2.RS
  N12: LCD2.R/W, LCM1602_IIC2.RW
  N13: LCD2.E, LCM1602_IIC2.E
  N14: LCD2.DB0, LCM1602_IIC2.D0
  N15: LCD2.DB1, LCM1602_IIC2.D1
  N16: LCD2.DB2, LCM1602_IIC2.D2
  N17: LCD2.DB3, LCM1602_IIC2.D3
  N18: LCD2.DB4, LCM1602_IIC2.D4
  N19: LCD2.DB5, LCM1602_IIC2.D5
  N20: LCD2.DB6, LCM1602_IIC2.D6
  N21: LCD2.DB7, LCM1602_IIC2.D7
  N22: LCD2.LED+, LCM1602_IIC2.A
  N23: LCD2.LED-, LCM1602_IIC2.K
  N24: LCM1602_IIC2.LED_A, LCM1602_IIC2.LED_B

custom parts:
  NodeMCU V3.0: ESP8266 based NodeMCU
  Keyes Relay: The Keyes 5V relay module is suitable for SCM development, home appliance control. It uses a 5V~12V TIL control signal which can control DC / AC signal.
  LCM1602 IIC: I2C-Module to use a 1602 or 2004 LCD on with the wire.h libory Serial LCD Modul
